# Fritzing sketch twenny (saved by Fritzing 0.9.4)

parts:
  U1 = ESP8266 NodeMCU LoLin module
  Grove1 = Grove OLED 128x96
  S1 = SWITCH-MOMENTARY-2 [package=tactile-pth-12mm]
  S2 = SWITCH-MOMENTARY-2 [package=tactile-pth-12mm]
  J1 = Piezo Speaker

nets:
  N1: U1.D1, Grove1.SDA
  N2: U1.D2, Grove1.SCL
  3V3: U1.3V3, Grove1.VCC
  GND: U1.GND, Grove1.GND, S1.1, S2.1, J1.pin1
  N3: U1.D5, J1.pin2
  N4: U1.D6, S2.2
  N5: U1.S3, S1.2

custom parts:
  ESP8266 NodeMCU LoLin module: ESP8266 based NodeMCU
